# Fritzing sketch 1-board (saved by Fritzing 0.9.9b)

parts:
  Part1 = Arduino Nano (Rev3.0)
  Squix1 = OLED 0.96" 128x64 I2C SSD1306
  Up = TTP223B Capacitive Touch Sensor Module
  Down = TTP223B Capacitive Touch Sensor Module
  Mode = TTP223B Capacitive Touch Sensor Module
  WeMos_D1_Mini_DC_Power_Shield1 = WeMos D1 Mini DC Power Shield
  12V = Power plug
  Fan_3 = Molex Picoblade Series Header [part_number=0533980471 package=Picoblade-53398-0471]
  Fan_2 = Molex Picoblade Series Header [part_number=0533980471 package=Picoblade-53398-0471]
  Fan_1 = Molex Picoblade Series Header [part_number=0533980471 package=Picoblade-53398-0471]
  Mod1 = Passive Buzzer
  3_5_mm = Audio Jack (TRRS) 3.5mm [part_number=DS18B20 package="RC-5325A [SMD]"]
  DS18B20 = IC, DIP package, 6 pins [part_number=adapter chip_label=IC]
  GY-906 = gy-906 [part_number=MLX90614]

nets:
  N1: Part1.D3, Fan_1.1
  N2: Part1.D4, Fan_1.2
  N3: Part1.D6, Mod1.S
  N4: Part1.D8, Fan_2.2
  N5: Part1.D9, Fan_2.1
  N6: Part1.D10, Fan_3.1
  N7: Part1.D11/MOSI, Fan_3.2
  VIN: Part1.VIN, WeMos_D1_Mini_DC_Power_Shield1.5V
  N8: Part1.GND, Mod1.-
  VCC: Part1.5V, Squix1.VCC, Up.VCC, Down.VCC, Mode.VCC, DS18B20.pin2, GY-906.VIN
  N9: Part1.A5, Squix1.SCL, GY-906.SCL
  N10: Part1.A4, Squix1.SCA, GY-906.SDA
  N11: Part1.A3, DS18B20.pin3
  N12: Part1.A2, Up.SIG
  N13: Part1.A1, Down.SIG
  N14: Part1.A0, Mode.SIG
  GND: Squix1.GND, Up.GND, Down.GND, Mode.GND, WeMos_D1_Mini_DC_Power_Shield1.G, 12V.GND, Fan_3.4, Fan_2.4, Fan_1.4, DS18B20.pin1, GY-906.GND
  12V: WeMos_D1_Mini_DC_Power_Shield1.12V, 12V.VCC, Fan_3.3, Fan_2.3, Fan_1.3
  N15: 3_5_mm.HOUSING, DS18B20.pin5
  N16: 3_5_mm.EARTH, DS18B20.pin4
  N17: 3_5_mm.RING, DS18B20.pin6

custom parts:
  TTP223B Capacitive Touch Sensor Module: The TTP223B capacitive touch sensor module uses the TTP223B IC. The appropriate voltage is approximately 2 to 5.5 volts.
  WeMos D1 Mini DC Power Shield: A DC Power shield.
  Audio Jack (TRRS) 3.5mm: Smartphone audio jack with 4 pins (stereo plus microphone), based on the Sparkfun PRT-12639
  gy-906: gy-906 Non-contact PIR I2C interface temperature sensor breakout board.
